// Logisim project !OLDarithmeticTEST.circ as structural Verilog: 1 circuit, main circuit autest
module autest (
  input  in_1
);

  wire arithmeticunit_1_carryout, arithmeticunit_1_overflow, bcd_to_7_segment_decoder_3_p1,
       bcd_to_7_segment_decoder_5_p1, bcd_to_7_segment_decoder_6_p1, binary_to_bcd_converter_1_p2,
       binary_to_bcd_converter_1_p4, binary_to_bcd_converter_2_p2;
  wire [1:0] undriven;
  wire [3:0] arithmeticunit_1_add_y, arithmeticunit_1_sub_y, dipswitch_1_p4, dipswitch_2_p4;

  // DipSwitch #(.number(4)) dipswitch_1: pin names not known; wires that end beside it: dipswitch_1_p4[3], dipswitch_1_p4[2], dipswitch_1_p4[1], dipswitch_1_p4[0]
  // DipSwitch #(.number(4)) dipswitch_2: pin names not known; wires that end beside it: dipswitch_2_p4[3], dipswitch_2_p4[2], dipswitch_2_p4[1], dipswitch_2_p4[0]
  // DipSwitch #(.number(2)) dipswitch_3: pin names not known
  arithmeticUnit arithmeticunit_1 (
    .Opcod(undriven), .CarryIn(in_1), .A(dipswitch_2_p4), .B(dipswitch_1_p4), .add_Y(arithmeticunit_1_add_y),
    .Sub_y(arithmeticunit_1_sub_y), .CarryOUT(arithmeticunit_1_carryout), .overflow(arithmeticunit_1_overflow));
  LED led_1 (.in(arithmeticunit_1_overflow));
  LED led_2 (.in(arithmeticunit_1_carryout));
  _7_Segment_Display u_7_segment_display_1 ();  // open: g, f, a, b, e, d, c, dp
  // BCD_to_7_Segment_decoder bcd_to_7_segment_decoder_1: pin names not known
  _7_Segment_Display u_7_segment_display_2 ();  // open: g, f, a, b, e, d, c, dp
  // BCD_to_7_Segment_decoder bcd_to_7_segment_decoder_2: pin names not known
  // Binary_to_BCD_converter binary_to_bcd_converter_1: pin names not known; wires that end beside it: {{5{1'b0}}, arithmeticunit_1_add_y}, binary_to_bcd_converter_1_p2, binary_to_bcd_converter_1_p2, binary_to_bcd_converter_1_p4
  _7_Segment_Display u_7_segment_display_3 ();  // open: g, f, a, b, e, d, c, dp
  // BCD_to_7_Segment_decoder bcd_to_7_segment_decoder_3: pin names not known; wires that end beside it: bcd_to_7_segment_decoder_3_p1
  // Binary_to_BCD_converter binary_to_bcd_converter_2: pin names not known; wires that end beside it: {{5{1'b0}}, arithmeticunit_1_sub_y}, binary_to_bcd_converter_2_p2, binary_to_bcd_converter_2_p2, bcd_to_7_segment_decoder_3_p1
  _7_Segment_Display u_7_segment_display_4 ();  // open: g, f, a, b, e, d, c, dp
  // BCD_to_7_Segment_decoder bcd_to_7_segment_decoder_4: pin names not known; wires that end beside it: binary_to_bcd_converter_1_p4
  _7_Segment_Display u_7_segment_display_5 ();  // open: g, f, a, b, e, d, c, dp
  // BCD_to_7_Segment_decoder bcd_to_7_segment_decoder_5: pin names not known; wires that end beside it: bcd_to_7_segment_decoder_5_p1, bcd_to_7_segment_decoder_5_p1
  _7_Segment_Display u_7_segment_display_6 ();  // open: g, f, a, b, e, d, c, dp
  // BCD_to_7_Segment_decoder bcd_to_7_segment_decoder_6: pin names not known; wires that end beside it: bcd_to_7_segment_decoder_6_p1, bcd_to_7_segment_decoder_6_p1

  // Notes on the sheet:
  //   decoded opCode
  //   negative
  //   and CarryOut in add
endmodule
