// Logisim project alu.circ as structural Verilog: 1 circuit, main circuit alu
module alu (
  input  [2:0] opC,
  input  Cin,
  input  [3:0] A,
  input  [3:0] B,
  output overflow,
  output Cout,
  output [7:0] Y
);

  wire n7408_1_pin3, n7408_1_pin6, n7408_1_pin8, n7408_1_pin11, n7408_3_pin3, n7408_3_pin6, n7408_3_pin8,
       n7408_3_pin11, n7408_4_pin3, n7408_4_pin6, n7408_4_pin8, n7408_4_pin11, n7432_1_pin2, n7432_1_pin3,
       n7432_1_pin5, n7432_1_pin6, n7432_1_pin8, n7432_1_pin10, n7432_1_pin11, n7432_1_pin12, n7432_3_pin3,
       n7432_3_pin6, n7432_3_pin8, n7432_3_pin11, n7432_4_pin3, n7432_4_pin6, n7432_4_pin8, n7432_4_pin11;
  wire [1:0] opcode_1_opcod;
  wire [2:0] opcode_1_opcod_2;
  wire [3:0] arithmeticunit_1_add_y, arithmeticunit_1_sub_y, logic_1_result0, logic_1_resulta,
       logic_1_resultx;
  wire [7:0] n7408_1_pin12;
  wire [7:2] n7408_1_pin1;

  _7408 u_7408_1 (
    .pin1(n7408_1_pin1[2]), .pin2(n7408_1_pin12[2]), .pin3(n7408_1_pin3), .pin4(n7408_1_pin12[3]),
    .pin5(n7408_1_pin1[2]), .pin6(n7408_1_pin6), .pin13(n7408_1_pin1[2]), .pin12(n7408_1_pin12[0]),
    .pin11(n7408_1_pin11), .pin10(n7408_1_pin1[2]), .pin9(n7408_1_pin12[1]), .pin8(n7408_1_pin8));
  _7408 u_7408_2 (
    .pin1(n7408_1_pin1[2]), .pin2(n7408_1_pin12[6]), .pin3(Y[6]), .pin4(n7408_1_pin12[7]),
    .pin5(n7408_1_pin1[2]), .pin6(Y[7]), .pin13(n7408_1_pin1[2]), .pin12(n7408_1_pin12[4]), .pin11(Y[4]),
    .pin10(n7408_1_pin1[2]), .pin9(n7408_1_pin12[5]), .pin8(Y[5]));
  bit4multiplier bit4multiplier_1 (.A(A), .B(B), .Y(n7408_1_pin12));
  OpCode opcode_1 (
    .A0(opC[0]), .A1(opC[1]), .A2(opC[2]),
    .Opcod({n7408_1_pin1[7], opcode_1_opcod_2, n7408_1_pin1[3:2], opcode_1_opcod}));
  arithmeticUnit arithmeticunit_1 (
    .Opcod(opcode_1_opcod), .CarryIn(Cin), .A(A), .B(B), .add_Y(arithmeticunit_1_add_y),
    .Sub_y(arithmeticunit_1_sub_y), .CarryOUT(overflow), .overflow(Cout));
  \logic  logic_1 (
    .Opcod(opcode_1_opcod_2), .A(A), .B(B), .resultA(logic_1_resulta), .result0(logic_1_result0),
    .resultX(logic_1_resultx));
  _7408 u_7408_3 (
    .pin1(arithmeticunit_1_add_y[2]), .pin2(opcode_1_opcod[0]), .pin3(n7408_3_pin3),
    .pin4(arithmeticunit_1_add_y[3]), .pin5(opcode_1_opcod[0]), .pin6(n7408_3_pin6),
    .pin13(arithmeticunit_1_add_y[0]), .pin12(opcode_1_opcod[0]), .pin11(n7408_3_pin11),
    .pin10(arithmeticunit_1_add_y[1]), .pin9(opcode_1_opcod[0]), .pin8(n7408_3_pin8));
  _7408 u_7408_4 (
    .pin1(arithmeticunit_1_sub_y[2]), .pin2(opcode_1_opcod[1]), .pin3(n7408_4_pin3),
    .pin4(arithmeticunit_1_sub_y[3]), .pin5(opcode_1_opcod[1]), .pin6(n7408_4_pin6),
    .pin13(arithmeticunit_1_sub_y[0]), .pin12(opcode_1_opcod[1]), .pin11(n7408_4_pin11),
    .pin10(arithmeticunit_1_sub_y[1]), .pin9(opcode_1_opcod[1]), .pin8(n7408_4_pin8));
  _7432 u_7432_1 (
    .pin1(logic_1_resultx[2]), .pin2(n7432_1_pin2), .pin3(n7432_1_pin3), .pin4(logic_1_resultx[3]),
    .pin5(n7432_1_pin5), .pin6(n7432_1_pin6), .pin13(logic_1_resultx[1]), .pin12(n7432_1_pin12),
    .pin11(n7432_1_pin11), .pin10(n7432_1_pin10), .pin9(logic_1_resultx[0]), .pin8(n7432_1_pin8));
  _7432 u_7432_2 (
    .pin1(logic_1_resulta[2]), .pin2(logic_1_result0[2]), .pin3(n7432_1_pin2), .pin4(logic_1_result0[3]),
    .pin5(logic_1_resulta[3]), .pin6(n7432_1_pin5), .pin13(logic_1_result0[1]), .pin12(logic_1_resulta[1]),
    .pin11(n7432_1_pin12), .pin10(logic_1_result0[0]), .pin9(logic_1_resulta[0]), .pin8(n7432_1_pin10));
  _7432 u_7432_3 (
    .pin1(n7408_3_pin3), .pin2(n7408_4_pin3), .pin3(n7432_3_pin3), .pin4(n7408_4_pin6), .pin5(n7408_3_pin6),
    .pin6(n7432_3_pin6), .pin13(n7408_3_pin11), .pin12(n7408_4_pin11), .pin11(n7432_3_pin11),
    .pin10(n7408_3_pin8), .pin9(n7408_4_pin8), .pin8(n7432_3_pin8));
  _7432 u_7432_4 (
    .pin1(n7432_3_pin3), .pin2(n7432_1_pin3), .pin3(n7432_4_pin3), .pin4(n7432_3_pin6), .pin5(n7432_1_pin6),
    .pin6(n7432_4_pin6), .pin13(n7432_3_pin11), .pin12(n7432_1_pin8), .pin11(n7432_4_pin11),
    .pin10(n7432_3_pin8), .pin9(n7432_1_pin11), .pin8(n7432_4_pin8));
  _7432 u_7432_5 (
    .pin1(n7432_4_pin8), .pin2(n7408_1_pin8), .pin3(Y[1]), .pin4(n7408_1_pin11), .pin5(n7432_4_pin11),
    .pin6(Y[0]), .pin13(n7432_4_pin3), .pin12(n7408_1_pin3), .pin11(Y[2]), .pin10(n7432_4_pin6),
    .pin9(n7408_1_pin6), .pin8(Y[3]));

  // Notes on the sheet:
  //   6
  //   0
  //   1
  //   4
  //   5
  //   7
  //   3
  //   2
  //   1
  //   2
  //   2
  //   1
  //   0
  //   temp0
  //   temp1
  //   temp3
  //   0
  //   1
  //   3
  //   2
  //   add
  //   1
  //   sub
  //   3
  //   2
  //   0
  //   3
  //   2
  //   3
  //   0
  //   1
  //   3
  //   2
  //   0
  //   1
  //   2
  //   3
  //   0
  //   2
  //   1
  //   3
endmodule
