// Logisim project arithmeticunit.circ as structural Verilog
module halfsub (
  input  a,
  input  b,
  output f,
  output out_4
);

  wire n7408_1_pin2, n7486_1_pin6;

  _7486 u_7486_1 (
    .pin1(a), .pin2(b), .pin3(f), .pin6(n7486_1_pin6), .pin9(n7486_1_pin6));  // open: pin4, pin5, pin13, pin12, pin11, pin10, pin8
  _7408 u_7408_1 (
    .pin1(b), .pin2(n7408_1_pin2), .pin3(out_4));  // open: pin4, pin5, pin6, pin13, pin12, pin11, pin10, pin9, pin8
  not not_1 (n7408_1_pin2, a);
endmodule

module fullsubraction (
  input  A,
  input  B,
  input  Bin,
  output D,
  output Bout
);

  wire halfsub_1_f, halfsub_1_out_4, halfsub_2_out_4;

  halfsub halfsub_1 (.a(A), .b(B), .f(halfsub_1_f), .out_4(halfsub_1_out_4));
  halfsub halfsub_2 (.a(halfsub_1_f), .b(Bin), .f(D), .out_4(halfsub_2_out_4));
  _7432 u_7432_1 (
    .pin1(halfsub_2_out_4), .pin2(halfsub_1_out_4), .pin3(Bout));  // open: pin4, pin5, pin6, pin13, pin12, pin11, pin10, pin9, pin8
endmodule

module fullsub (
  input  [3:0] A,
  input  [3:0] B,
  input  BorrowIn,
  output [3:0] Y,
  output borrow
);

  wire fullsubraction_1_bout, fullsubraction_2_bout, fullsubraction_3_bout;

  fullsubraction fullsubraction_1 (.A(A[0]), .B(B[0]), .Bin(BorrowIn), .D(Y[0]), .Bout(fullsubraction_1_bout));
  fullsubraction fullsubraction_2 (
    .A(A[1]), .B(B[1]), .Bin(fullsubraction_1_bout), .D(Y[1]), .Bout(fullsubraction_2_bout));
  fullsubraction fullsubraction_3 (
    .A(A[2]), .B(B[2]), .Bin(fullsubraction_2_bout), .D(Y[2]), .Bout(fullsubraction_3_bout));
  fullsubraction fullsubraction_4 (.A(A[3]), .B(B[3]), .Bin(fullsubraction_3_bout), .D(Y[3]), .Bout(borrow));
endmodule

module OpCode (
  input  A0,
  input  A1,
  input  A2,
  output [7:0] Opcod
);

  wire n7408_1_pin3, n7408_1_pin6, n7408_1_pin8, n7408_1_pin11, not_1_out, not_2_out, not_3_out;

  not not_1 (not_1_out, A0);
  not not_2 (not_2_out, A1);
  not not_3 (not_3_out, A2);
  _7408 u_7408_1 (
    .pin1(A2), .pin2(A1), .pin3(n7408_1_pin3), .pin4(not_3_out), .pin5(A1), .pin6(n7408_1_pin6), .pin13(A2),
    .pin12(not_2_out), .pin11(n7408_1_pin11), .pin10(not_3_out), .pin9(not_2_out), .pin8(n7408_1_pin8));
  _7408 u_7408_2 (
    .pin1(not_1_out), .pin2(n7408_1_pin8), .pin3(Opcod[0]), .pin4(n7408_1_pin8), .pin5(A0), .pin6(Opcod[1]),
    .pin13(n7408_1_pin6), .pin12(not_1_out), .pin11(Opcod[2]), .pin10(n7408_1_pin6), .pin9(A0),
    .pin8(Opcod[3]));
  _7408 u_7408_3 (
    .pin1(n7408_1_pin11), .pin2(not_1_out), .pin3(Opcod[4]), .pin4(n7408_1_pin11), .pin5(A0),
    .pin6(Opcod[5]), .pin13(n7408_1_pin3), .pin12(not_1_out), .pin11(Opcod[6]), .pin10(n7408_1_pin3),
    .pin9(A0), .pin8(Opcod[7]));

  // Notes on the sheet:
  //   notc
  //   notb
  //   nota
  //   and3
endmodule

module \logic  (
  input  [2:0] Opcod,
  input  [3:0] A,
  input  [3:0] B,
  output [3:0] resultA,
  output [3:0] result0,
  output [3:0] resultX
);

  wire n7408_1_pin3, n7408_1_pin6, n7408_1_pin8, n7408_1_pin11, n7432_1_pin3, n7432_1_pin6, n7432_1_pin8,
       n7432_1_pin11, n7486_1_pin3, n7486_1_pin6, n7486_1_pin8, n7486_1_pin11;

  _7408 u_7408_1 (
    .pin1(A[0]), .pin2(B[0]), .pin3(n7408_1_pin3), .pin4(B[1]), .pin5(A[1]), .pin6(n7408_1_pin6),
    .pin13(A[2]), .pin12(B[2]), .pin11(n7408_1_pin11), .pin10(A[3]), .pin9(B[3]), .pin8(n7408_1_pin8));
  _7432 u_7432_1 (
    .pin1(A[0]), .pin2(B[0]), .pin3(n7432_1_pin3), .pin4(A[1]), .pin5(B[1]), .pin6(n7432_1_pin6),
    .pin13(A[2]), .pin12(B[2]), .pin11(n7432_1_pin11), .pin10(A[3]), .pin9(B[3]), .pin8(n7432_1_pin8));
  _7486 u_7486_1 (
    .pin1(A[0]), .pin2(B[0]), .pin3(n7486_1_pin3), .pin4(A[1]), .pin5(B[1]), .pin6(n7486_1_pin6),
    .pin13(A[2]), .pin12(B[2]), .pin11(n7486_1_pin11), .pin10(A[3]), .pin9(B[3]), .pin8(n7486_1_pin8));
  _7408 u_7408_2 (
    .pin1(Opcod[0]), .pin2(n7408_1_pin3), .pin3(resultA[0]), .pin4(Opcod[0]), .pin5(n7408_1_pin6),
    .pin6(resultA[1]), .pin13(Opcod[0]), .pin12(n7408_1_pin11), .pin11(resultA[2]), .pin10(Opcod[0]),
    .pin9(n7408_1_pin8), .pin8(resultA[3]));
  _7408 u_7408_3 (
    .pin1(Opcod[1]), .pin2(n7432_1_pin3), .pin3(result0[0]), .pin4(Opcod[1]), .pin5(n7432_1_pin6),
    .pin6(result0[1]), .pin13(Opcod[1]), .pin12(n7432_1_pin11), .pin11(result0[2]), .pin10(Opcod[1]),
    .pin9(n7432_1_pin8), .pin8(result0[3]));
  _7408 u_7408_4 (
    .pin1(Opcod[2]), .pin2(n7486_1_pin3), .pin3(resultX[0]), .pin4(Opcod[2]), .pin5(n7486_1_pin6),
    .pin6(resultX[1]), .pin13(Opcod[2]), .pin12(n7486_1_pin11), .pin11(resultX[2]), .pin10(Opcod[2]),
    .pin9(n7486_1_pin8), .pin8(resultX[3]));

  // Notes on the sheet:
  //   IN1
  //   IN2
  //   and12
  //   and10
  //   and13
  //   and11
  //   or12
  //   or10
  //   or13
  //   or11
  //   xor10
  //   xor12
  //   xor11
  //   xor13
  //   resultA0
  //   resultA1
  //   result02
  //   result00
  //   result03
  //   resul01
  //   resultX0
  //   resultX3
  //   resultX2
  //   resultX1
  //   resultA
  //   result0
  //   resultX
endmodule

module addition (
  input  cin,
  input  [3:0] A,
  input  [3:0] B,
  output [3:0] Y,
  output CarryOut,
  output overflow
);

  wire fulladd_1_cout, fulladd_2_cout, fulladd_3_cout;

  fulladd fulladd_1 (.A(A[0]), .B(B[0]), .Carry(cin), .sum(Y[0]), .Cout(fulladd_1_cout));
  fulladd fulladd_2 (.A(A[1]), .B(B[1]), .Carry(fulladd_1_cout), .sum(Y[1]), .Cout(fulladd_2_cout));
  fulladd fulladd_3 (.A(A[2]), .B(B[2]), .Carry(fulladd_2_cout), .sum(Y[2]), .Cout(fulladd_3_cout));
  fulladd fulladd_4 (.A(A[3]), .B(B[3]), .Carry(fulladd_3_cout), .sum(Y[3]), .Cout(CarryOut));
  xor xor_1 (overflow, CarryOut, fulladd_3_cout);
endmodule

module fulladd (
  input  A,
  input  B,
  input  Carry,
  output sum,
  output Cout
);

  wire and_1_out, and_2_out, xor_1_out;

  xor xor_1 (xor_1_out, A, B);
  xor xor_2 (sum, xor_1_out, Carry);
  and and_1 (and_1_out, xor_1_out, Carry);
  and and_2 (and_2_out, B, A);
  or or_1 (Cout, and_1_out, and_2_out);
endmodule

module arithmeticUnit (
  input  [1:0] Opcod,
  input  CarryIn,
  input  [3:0] A,
  input  [3:0] B,
  output [3:0] add_Y,
  output [3:0] Sub_y,
  output CarryOUT,
  output overflow
);

  wire n7408_1_pin2, n7408_1_pin8, n7408_1_pin9, n7408_1_pin11, n7408_1_pin13;
  wire [3:0] addition_1_y, fullsub_1_y;

  _7408 u_7408_1 (
    .pin1(Opcod[0]), .pin2(n7408_1_pin2), .pin3(overflow), .pin13(n7408_1_pin13), .pin12(Opcod[0]),
    .pin11(n7408_1_pin11), .pin10(Opcod[1]), .pin9(n7408_1_pin9), .pin8(n7408_1_pin8));  // open: pin4, pin5, pin6
  addition addition_1 (
    .cin(CarryIn), .A(A), .B(B), .Y(addition_1_y), .CarryOut(n7408_1_pin13), .overflow(n7408_1_pin2));
  fullsub fullsub_1 (.A(A), .B(B), .BorrowIn(CarryIn), .Y(fullsub_1_y), .borrow(n7408_1_pin9));
  // _7432 7432_1: pin names not known; wires that end beside it: 1'b1, n7408_1_pin11, n7408_1_pin8, CarryOUT, 1'b0
  _7408 u_7408_2 (
    .pin1(addition_1_y[2]), .pin2(Opcod[0]), .pin3(add_Y[2]), .pin4(Opcod[0]), .pin5(addition_1_y[3]),
    .pin6(add_Y[3]), .pin13(addition_1_y[0]), .pin12(Opcod[0]), .pin11(add_Y[0]), .pin10(addition_1_y[1]),
    .pin9(Opcod[0]), .pin8(add_Y[1]));
  _7408 u_7408_3 (
    .pin1(fullsub_1_y[2]), .pin2(Opcod[1]), .pin3(Sub_y[2]), .pin4(Opcod[1]), .pin5(fullsub_1_y[3]),
    .pin6(Sub_y[3]), .pin13(fullsub_1_y[0]), .pin12(Opcod[1]), .pin11(Sub_y[0]), .pin10(Opcod[1]),
    .pin9(fullsub_1_y[1]), .pin8(Sub_y[1]));

  // Notes on the sheet:
  //   opCoded CarryO
  //   add_Y0
  //   addy_2
  //   sub_y0
  //   sub_y2
  //   add_y1
  //   add_y3
  //   sub_y1
  //   sub_y3
endmodule
