// Logisim project autest.circ as structural Verilog: 1 circuit, main circuit main
module main (
  input  in_1
);

  wire arithmeticunit_1_carryout, arithmeticunit_1_overflow, bcd_to_7_segment_decoder_3_p1,
       bcd_to_7_segment_decoder_6_p1, bcd_to_7_segment_decoder_9_p1, bcd_to_7_segment_decoder_12_p1,
       binary_to_bcd_converter_1_p2, binary_to_bcd_converter_1_p4, binary_to_bcd_converter_2_p2,
       binary_to_bcd_converter_2_p4, binary_to_bcd_converter_3_p2, binary_to_bcd_converter_3_p4,
       binary_to_bcd_converter_4_p3, binary_to_bcd_converter_4_p5;
  wire [1:0] dipswitch_1_sw2;
  wire [3:0] arithmeticunit_1_add_y, arithmeticunit_1_sub_y, dipswitch_2_p4, dipswitch_2_p8;

  DipSwitch #(.number(2)) dipswitch_1 (.sw1(dipswitch_1_sw2[1]), .sw2(dipswitch_1_sw2[0]));
  // DipSwitch dipswitch_2: pin names not known; wires that end beside it: dipswitch_2_p4[3], dipswitch_2_p4[2], dipswitch_2_p4[1], dipswitch_2_p4[0], dipswitch_2_p8[3], dipswitch_2_p8[2], dipswitch_2_p8[1], dipswitch_2_p8[0]
  _7_Segment_Display u_7_segment_display_1 ();  // open: g, f, a, b, e, d, c, dp
  // BCD_to_7_Segment_decoder bcd_to_7_segment_decoder_1: pin names not known
  // Binary_to_BCD_converter binary_to_bcd_converter_1: pin names not known; wires that end beside it: {{5{1'b0}}, dipswitch_2_p8}, binary_to_bcd_converter_1_p2, binary_to_bcd_converter_1_p2, binary_to_bcd_converter_1_p4
  _7_Segment_Display u_7_segment_display_2 ();  // open: g, f, a, b, e, d, c, dp
  // BCD_to_7_Segment_decoder bcd_to_7_segment_decoder_2: pin names not known; wires that end beside it: binary_to_bcd_converter_1_p4
  _7_Segment_Display u_7_segment_display_3 ();  // open: g, f, a, b, e, d, c, dp
  // BCD_to_7_Segment_decoder bcd_to_7_segment_decoder_3: pin names not known; wires that end beside it: bcd_to_7_segment_decoder_3_p1, bcd_to_7_segment_decoder_3_p1
  arithmeticUnit arithmeticunit_1 (
    .Opcod(dipswitch_1_sw2), .CarryIn(in_1), .A(dipswitch_2_p8), .B(dipswitch_2_p4),
    .add_Y(arithmeticunit_1_add_y), .Sub_y(arithmeticunit_1_sub_y), .CarryOUT(arithmeticunit_1_carryout),
    .overflow(arithmeticunit_1_overflow));
  LED led_1 (.in(arithmeticunit_1_overflow));
  _7_Segment_Display u_7_segment_display_4 ();  // open: g, f, a, b, e, d, c, dp
  // BCD_to_7_Segment_decoder bcd_to_7_segment_decoder_4: pin names not known
  // Binary_to_BCD_converter binary_to_bcd_converter_2: pin names not known; wires that end beside it: {{5{1'b0}}, dipswitch_2_p4}, binary_to_bcd_converter_2_p2, binary_to_bcd_converter_2_p2, binary_to_bcd_converter_2_p4
  LED led_2 (.in(arithmeticunit_1_carryout));
  _7_Segment_Display u_7_segment_display_5 ();  // open: g, f, a, b, e, d, c, dp
  _7_Segment_Display u_7_segment_display_6 ();  // open: g, f, a, b, e, d, c, dp
  // BCD_to_7_Segment_decoder bcd_to_7_segment_decoder_5: pin names not known; wires that end beside it: binary_to_bcd_converter_2_p4
  // BCD_to_7_Segment_decoder bcd_to_7_segment_decoder_6: pin names not known; wires that end beside it: bcd_to_7_segment_decoder_6_p1, bcd_to_7_segment_decoder_6_p1
  _7_Segment_Display u_7_segment_display_7 ();  // open: g, f, a, b, e, d, c, dp
  // BCD_to_7_Segment_decoder bcd_to_7_segment_decoder_7: pin names not known
  // Binary_to_BCD_converter binary_to_bcd_converter_3: pin names not known; wires that end beside it: {{5{1'b0}}, arithmeticunit_1_add_y}, binary_to_bcd_converter_3_p2, binary_to_bcd_converter_3_p2, binary_to_bcd_converter_3_p4
  _7_Segment_Display u_7_segment_display_8 ();  // open: g, f, a, b, e, d, c, dp
  // BCD_to_7_Segment_decoder bcd_to_7_segment_decoder_8: pin names not known; wires that end beside it: binary_to_bcd_converter_3_p4
  _7_Segment_Display u_7_segment_display_9 ();  // open: g, f, a, b, e, d, c, dp
  // BCD_to_7_Segment_decoder bcd_to_7_segment_decoder_9: pin names not known; wires that end beside it: bcd_to_7_segment_decoder_9_p1, bcd_to_7_segment_decoder_9_p1
  _7_Segment_Display u_7_segment_display_10 ();  // open: g, f, a, b, e, d, c, dp
  // BCD_to_7_Segment_decoder bcd_to_7_segment_decoder_10: pin names not known
  // Binary_to_BCD_converter binary_to_bcd_converter_4: pin names not known; wires that end beside it: 1'b0, {{5{1'b0}}, arithmeticunit_1_sub_y}, binary_to_bcd_converter_4_p3, binary_to_bcd_converter_4_p3, binary_to_bcd_converter_4_p5
  _7_Segment_Display u_7_segment_display_11 ();  // open: g, f, a, b, e, d, c, dp
  // BCD_to_7_Segment_decoder bcd_to_7_segment_decoder_11: pin names not known; wires that end beside it: binary_to_bcd_converter_4_p5
  _7_Segment_Display u_7_segment_display_12 ();  // open: g, f, a, b, e, d, c, dp
  // BCD_to_7_Segment_decoder bcd_to_7_segment_decoder_12: pin names not known; wires that end beside it: bcd_to_7_segment_decoder_12_p1, bcd_to_7_segment_decoder_12_p1

  // Notes on the sheet:
  //   switch 2 add
  //   switch 1 sub
  //   decoded opcode
  //   A
  //   B
endmodule
