// Logisim project multiplier4.circ as structural Verilog: 3 circuits, main circuit bit4multiplier
module bit4multiplier (
  input  [3:0] A,
  input  [3:0] B,
  output [7:0] Y
);

  wire [2:0] n7408_1_pin8;
  wire [3:0] addition4_1_carryo, n7408_2_pin11, n7408_3_pin11, n7408_4_pin11;
  wire [3:1] addition4_2_sum;
  wire [3:3] addition4_2_carryo;

  _7408 u_7408_1 (
    .pin1(B[0]), .pin2(A[2]), .pin3(n7408_1_pin8[1]), .pin4(B[0]), .pin5(A[3]), .pin6(n7408_1_pin8[2]),
    .pin13(B[0]), .pin12(A[0]), .pin11(Y[0]), .pin10(B[0]), .pin9(A[1]), .pin8(n7408_1_pin8[0]));
  _7408 u_7408_2 (
    .pin1(A[2]), .pin2(B[2]), .pin3(n7408_2_pin11[2]), .pin4(B[2]), .pin5(A[3]), .pin6(n7408_2_pin11[3]),
    .pin13(A[0]), .pin12(B[2]), .pin11(n7408_2_pin11[0]), .pin10(A[1]), .pin9(B[2]), .pin8(n7408_2_pin11[1]));
  _7408 u_7408_3 (
    .pin1(B[3]), .pin2(A[2]), .pin3(n7408_3_pin11[2]), .pin4(A[3]), .pin5(B[3]), .pin6(n7408_3_pin11[3]),
    .pin13(A[0]), .pin12(B[3]), .pin11(n7408_3_pin11[0]), .pin10(A[1]), .pin9(B[3]), .pin8(n7408_3_pin11[1]));
  _7408 u_7408_4 (
    .pin1(A[2]), .pin2(B[1]), .pin3(n7408_4_pin11[2]), .pin4(A[3]), .pin5(B[1]), .pin6(n7408_4_pin11[3]),
    .pin13(A[0]), .pin12(B[1]), .pin11(n7408_4_pin11[0]), .pin10(A[1]), .pin9(B[1]), .pin8(n7408_4_pin11[1]));
  addition4 addition4_1 (
    .CarryIn(1'b0), .A(n7408_4_pin11), .B({1'b0, n7408_1_pin8}), .Sum({addition4_1_carryo[2:0], Y[1]}),
    .CarryO(addition4_1_carryo[3]));
  addition4 addition4_2 (
    .CarryIn(1'b0), .A(n7408_2_pin11), .B(addition4_1_carryo), .Sum({addition4_2_sum, Y[2]}),
    .CarryO(addition4_2_carryo[3]));
  addition4 addition4_3 (
    .CarryIn(1'b0), .A(n7408_3_pin11), .B({addition4_2_carryo[3], addition4_2_sum}), .Sum(Y[6:3]),
    .CarryO(Y[7]));
endmodule

module fulladder (
  input  Cin,
  input  A,
  input  B,
  output Sum,
  output CarryO
);

  wire n7408_1_pin10, n7432_1_p2, n7432_1_p3;

  // _7432 7432_1: pin names not known; wires that end beside it: 1'b1, n7432_1_p2, n7432_1_p3, CarryO, 1'b0
  _7408 u_7408_1 (
    .pin13(A), .pin12(B), .pin11(n7432_1_p2), .pin10(n7408_1_pin10), .pin9(Cin), .pin8(n7432_1_p3));  // open: pin1, pin2, pin3, pin4, pin5, pin6
  _7486 u_7486_1 (
    .pin13(B), .pin12(A), .pin11(n7408_1_pin10), .pin10(n7408_1_pin10), .pin9(Cin), .pin8(Sum));  // open: pin1, pin2, pin3, pin4, pin5, pin6
endmodule

module addition4 (
  input  CarryIn,
  input  [3:0] A,
  input  [3:0] B,
  output [3:0] Sum,
  output CarryO
);

  wire fulladder_1_carryo, fulladder_2_carryo, fulladder_3_carryo;

  fulladder fulladder_1 (.Cin(CarryIn), .A(A[0]), .B(B[0]), .Sum(Sum[0]), .CarryO(fulladder_1_carryo));
  fulladder fulladder_2 (.Cin(fulladder_1_carryo), .A(A[1]), .B(B[1]), .Sum(Sum[1]), .CarryO(fulladder_2_carryo));
  fulladder fulladder_3 (.Cin(fulladder_2_carryo), .A(A[2]), .B(B[2]), .Sum(Sum[2]), .CarryO(fulladder_3_carryo));
  fulladder fulladder_4 (.Cin(fulladder_3_carryo), .A(A[3]), .B(B[3]), .Sum(Sum[3]), .CarryO(CarryO));
endmodule
