// Logisim project opCode.circ as structural Verilog: 1 circuit, main circuit main
module main (
);

  wire and_1_out, and_2_out, and_3_out, and_4_out, and_5_out, and_6_out, and_7_out, and_8_out, and_9_out,
       and_10_out, and_11_out, and_12_out, dipswitch_1_p1, dipswitch_1_p2, dipswitch_1_p3, not_1_out,
       not_2_out, not_3_out;

  // DipSwitch dipswitch_1: pin names not known; wires that end beside it: dipswitch_1_p1, dipswitch_1_p2, dipswitch_1_p3
  not not_1 (not_1_out, dipswitch_1_p3);
  not not_2 (not_2_out, dipswitch_1_p2);
  and and_1 (and_1_out, not_1_out, not_2_out);
  and and_2 (and_2_out, not_1_out, dipswitch_1_p2);
  and and_3 (and_3_out, dipswitch_1_p3, not_2_out);
  and and_4 (and_4_out, dipswitch_1_p3, dipswitch_1_p2);
  not not_3 (not_3_out, dipswitch_1_p1);
  and and_5 (and_5_out, and_1_out, not_3_out);
  and and_6 (and_6_out, and_1_out, dipswitch_1_p1);
  and and_7 (and_7_out, and_2_out, not_3_out);
  and and_8 (and_8_out, and_2_out, dipswitch_1_p1);
  and and_9 (and_9_out, and_3_out, not_3_out);
  and and_10 (and_10_out, and_3_out, dipswitch_1_p1);
  and and_11 (and_11_out, and_4_out, not_3_out);
  and and_12 (and_12_out, and_4_out, dipswitch_1_p1);
  LedBar ledbar_1 (
    .led0(and_5_out), .led1(and_6_out), .led2(and_7_out), .led3(and_8_out), .led4(and_9_out),
    .led5(and_10_out), .led6(and_11_out), .led7(and_12_out));
endmodule
