// Logisim project subraction.circ as structural Verilog
module opcode (
  input  A0,
  input  A1,
  input  A2,
  output opcode2,
  output opcode3,
  output opcode1,
  output opcode0,
  output opcode6,
  output opcode7,
  output opcode5,
  output opcode4
);

  wire n7408_1_pin3, n7408_1_pin6, n7408_1_pin8, n7408_1_pin11, not_1_out, not_2_out, not_3_out;

  not not_1 (not_1_out, A0);
  not not_2 (not_2_out, A1);
  not not_3 (not_3_out, A2);
  _7408 u_7408_1 (
    .pin1(A2), .pin2(A1), .pin3(n7408_1_pin3), .pin4(not_3_out), .pin5(A1), .pin6(n7408_1_pin6), .pin13(A2),
    .pin12(not_2_out), .pin11(n7408_1_pin11), .pin10(not_3_out), .pin9(not_2_out), .pin8(n7408_1_pin8));
  _7408 u_7408_2 ();  // open: pin1, pin2, pin3, pin4, pin5, pin6, pin13, pin12, pin11, pin10, pin9, pin8
  _7408 u_7408_3 (
    .pin1(not_1_out), .pin2(n7408_1_pin8), .pin3(opcode0), .pin4(n7408_1_pin8), .pin5(A0), .pin6(opcode1),
    .pin13(n7408_1_pin6), .pin12(not_1_out), .pin11(opcode2), .pin10(n7408_1_pin6), .pin9(A0), .pin8(opcode3));
  _7408 u_7408_4 (
    .pin1(n7408_1_pin11), .pin2(not_1_out), .pin3(opcode4), .pin4(n7408_1_pin11), .pin5(A0), .pin6(opcode5),
    .pin13(n7408_1_pin3), .pin12(not_1_out), .pin11(opcode6), .pin10(n7408_1_pin3), .pin9(A0), .pin8(opcode7));

  // Notes on the sheet:
  //   notc
  //   notb
  //   nota
  //   and3
endmodule
